# Fritzing sketch midimutant (saved by Fritzing 0.8.5b)
circuit board: 3.65266cm x 2.57955cm
breadboards: 1

parts:
  74HC14 = Hex Inverter Schmitt Trigger SN74HC14 [package="DIP (Dual Inline)"]
  R1 = Resistor [tolerance=±5% resistance=220 package=THT]
  R2 = Resistor [tolerance=±5% resistance=220 package=THT]
  J2 = female pin header, 6 pins [form="♀ (female)"]

nets:
  N1: 74HC14.1A, 74HC14.6Y
  N2: 74HC14.1Y, R1.Pin_1
  N3: 74HC14.GND, J2.pin3, J2.pin4
  N4: 74HC14.6A, J2.pin6
  N5: 74HC14.VCC, R2.Pin_1, J2.pin5
  N6: R1.Pin_0, J2.pin1
  N7: R2.Pin_0, J2.pin2

notes:
  midimutant 0.1
  midimutant
